# Fritzing sketch elec diagram (saved by Fritzing 1.0.5)
breadboards: 1

parts:
  Pico/Pico2_Mod_1 = Raspberry Pi Pico or Pico 2
  J1 = Basic Servo
  A1 = AS5600 module
  X-axis = Rotary Potentiometer (Large) [maximum_resistance=100kΩ knob_status=50% power=0.5W package=THT]
  Y-axis1 = Rotary Potentiometer (Large) [maximum_resistance=100kΩ knob_status=50% power=0.5W package=THT]
  VCC1 = 4 x AAA Battery Mount [internal_resistance=0.1Ω]
  A2 = AS5600 module
  A3 = AS5600 module
  A4 = AS5600 module
  A5 = AS5600 module
  Multiplexer = Adafruit TCA9548A
  U1 = SWITCH-SPST-2 [package=r_sw_th]
  U2 = SWITCH-SPST-2 [package=r_sw_th]
  U3 = SWITCH-SPST-2 [package=r_sw_th]

nets:
  GND: Pico/Pico2_Mod_1.pin_3, Pico/Pico2_Mod_1.pin_18, Pico/Pico2_Mod_1.pin_38, J1.gnd, A1.Pin_3, X-axis.leg2, Y-axis1.leg2, VCC1.-, A2.Pin_3, A3.Pin_3, A4.Pin_3, A5.Pin_3, Multiplexer.GND
  N1: Pico/Pico2_Mod_1.pin_6, Multiplexer.INPUTSDA
  N2: Pico/Pico2_Mod_1.pin_7, Multiplexer.INPUTSCL
  N3: Pico/Pico2_Mod_1.pin_20, J1.pulse
  N4: Pico/Pico2_Mod_1.pin_24, U3.P
  N5: Pico/Pico2_Mod_1.pin_25, U2.P
  N6: Pico/Pico2_Mod_1.pin_26, U1.P
  N7: Pico/Pico2_Mod_1.pin_31, Y-axis1.wiper
  N8: Pico/Pico2_Mod_1.pin_32, X-axis.wiper
  N9: Pico/Pico2_Mod_1.pin_36, A1.Pin_1, X-axis.leg1, Y-axis1.leg1, A2.Pin_1, A3.Pin_1, A4.Pin_1, A5.Pin_1, Multiplexer.VCC, U1.O, U2.O, U3.O
  N10: J1.vcc, VCC1.+
  N11: A1.Pin_5, Multiplexer.0SDA
  N12: A1.Pin_6, Multiplexer.0SCL
  N13: A2.Pin_5, Multiplexer.1SDA
  N14: A2.Pin_6, Multiplexer.1SCL
  N15: A3.Pin_5, Multiplexer.2SDA
  N16: A3.Pin_6, Multiplexer.2SCL
  N17: A4.Pin_5, Multiplexer.3SDA
  N18: A4.Pin_6, Multiplexer.3SCL
  N19: A5.Pin_5, Multiplexer.4SDA
  N20: A5.Pin_6, Multiplexer.4SCL

custom parts:
  Raspberry Pi Pico or Pico 2: Raspberry Pi Pico and Pico 2. Based around the RP2040 and RP2350 microcontrollers respectively, Picos are low cost microcontroller device bringing Raspberry Pi quality, cost, and easy of use to the microcontroller space. Jan 2021, Split part in to two versions: tht (this one) and SMD. This one will drill holes for a .1 in header in pcb to allow plugging in the module as well as providing pads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
  AS5600 module: .This module is mainly placed behind the stepper motor to obtain the rotation angle of the stepper motor.
  Adafruit TCA9548A: You just found the perfect I2C sensor, and you want to wire up two or three or more of them to your Arduino when you realize "Uh oh, this chip has a fixed I2C address, and from what I know about I2C, you cannot have two devices with the same address on the same SDA/SCL pins!" Are you out of luck? You would be, if you didn't have this ultra-cool TCA9548A 1-to-8 I2C multiplexer! Finally, a way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
